// Logisim project Zadanie 1 — kopia.circ as structural Verilog
module main (
  input  in_1,
  input  in_2,
  input  in_3,
  input  in_4
);

  wire dekoder_1_a, dekoder_1_b, dekoder_1_c, dekoder_1_d, dekoder_1_e, dekoder_1_f, dekoder_1_g;

  dekoder dekoder_1 (
    .x(in_1), .y(in_2), .w(in_3), .z(in_4), .a(dekoder_1_a), .b(dekoder_1_b), .c(dekoder_1_c),
    .d(dekoder_1_d), .e(dekoder_1_e), .f(dekoder_1_f), .g(dekoder_1_g));
  _7_Segment_Display u_7_segment_display_1 (
    .g(dekoder_1_d), .f(dekoder_1_c), .a(dekoder_1_b), .b(dekoder_1_a), .e(dekoder_1_e), .d(dekoder_1_f),
    .c(dekoder_1_g));  // open: dp
endmodule

module a (
  input  x,
  input  y,
  input  w,
  input  z,
  output out_5
);

  wire or_1_out, or_2_out;

  or or_1 (or_1_out, x, ~y, w, ~z);  // OR_Gate
  or or_2 (or_2_out, x, ~y, ~w, z);  // OR_Gate
  and and_1 (out_5, or_1_out, or_2_out);
endmodule

module dekoder (
  input  x,
  input  y,
  input  w,
  input  z,
  output a,
  output b,
  output c,
  output d,
  output e,
  output f,
  output g
);

  a a_1 (.x(x), .y(y), .w(w), .z(z), .out_5(a));
  b b_1 (.x(x), .y(y), .w(w), .z(z), .out_5(b));
  c c_1 (.x(x), .y(y), .w(w), .z(z), .out_5(c));
  d d_1 (.x(x), .y(y), .w(w), .z(z), .out_5(d));
  e e_1 (.x(x), .y(y), .w(w), .z(z), .out_5(e));
  f f_1 (.x(x), .y(y), .w(w), .z(z), .out_5(f));
  g g_1 (.x(x), .y(y), .w(w), .z(z), .out_5(g));
endmodule

module b (
  input  x,
  input  y,
  input  w,
  input  z,
  output out_5
);

  wire or_1_out, or_2_out;

  or or_1 (or_1_out, x, ~y, w, z);  // OR_Gate
  or or_2 (or_2_out, x, y, w, ~z);  // OR_Gate
  and and_1 (out_5, or_1_out, or_2_out);
endmodule

module c (
  input  x,
  input  y,
  input  w,
  input  z,
  output out_5
);

  wire and_1_out, and_2_out, and_3_out;

  and and_1 (and_1_out, ~w, ~z);  // AND_Gate
  and and_2 (and_2_out, y, ~w);  // AND_Gate
  and and_3 (and_3_out, y, ~z);  // AND_Gate
  or or_1 (out_5, x, and_1_out, and_2_out, and_3_out);
endmodule

module d (
  input  x,
  input  y,
  input  w,
  input  z,
  output out_5
);

  wire and_1_out, and_2_out, and_3_out;

  and and_1 (and_1_out, ~y, w);  // AND_Gate
  and and_2 (and_2_out, w, ~z);  // AND_Gate
  and and_3 (and_3_out, y, ~w);  // AND_Gate
  or or_1 (out_5, x, and_1_out, and_2_out, and_3_out);
endmodule

module e (
  input  x,
  input  y,
  input  w,
  input  z,
  output out_5
);

  wire and_1_out, and_2_out;

  and and_1 (and_1_out, ~y, ~z);  // AND_Gate
  and and_2 (and_2_out, w, ~z);  // AND_Gate
  or or_1 (out_5, and_1_out, and_2_out);
endmodule

module f (
  input  x,
  input  y,
  input  w,
  input  z,
  output out_5
);

  wire and_1_out, and_2_out, and_3_out, and_4_out;

  and and_1 (and_1_out, ~y, ~z);  // AND_Gate
  and and_2 (and_2_out, ~y, w);  // AND_Gate
  and and_3 (and_3_out, w, ~z);  // AND_Gate
  and and_4 (and_4_out, y, ~w, z);  // AND_Gate
  or or_1 (out_5, x, and_1_out, and_2_out, and_3_out, and_4_out);
endmodule

module g (
  input  x,
  input  y,
  input  w,
  input  z,
  output out_5
);

  or or_1 (out_5, ~w, z, y, x);  // OR_Gate
endmodule

module Zadanie_2 (
);

  wire and_1_out, clock_1_out, d_ff_1_q, d_ff_1_qn, d_ff_2_q, d_ff_2_qn, d_ff_3_q, d_ff_3_qn, d_ff_4_q,
       d_ff_4_qn, dekoder_1_a, dekoder_1_b, dekoder_1_c, dekoder_1_d, dekoder_1_e, dekoder_1_f, dekoder_1_g;

  Clock clock_1 (.out(clock_1_out));
  D_Flip_Flop d_ff_1 (
    .clk(clock_1_out), .D(d_ff_1_qn), .Q(d_ff_1_q), .Qn(d_ff_1_qn), .reset(and_1_out));  // open: preset, en
  D_Flip_Flop d_ff_2 (
    .clk(d_ff_1_qn), .D(d_ff_2_qn), .Q(d_ff_2_q), .Qn(d_ff_2_qn), .reset(and_1_out));  // open: preset, en
  dekoder dekoder_1 (
    .x(d_ff_4_q), .y(d_ff_3_q), .w(d_ff_2_q), .z(d_ff_1_q), .a(dekoder_1_a), .b(dekoder_1_b),
    .c(dekoder_1_c), .d(dekoder_1_d), .e(dekoder_1_e), .f(dekoder_1_f), .g(dekoder_1_g));
  and and_1 (and_1_out, d_ff_2_q, d_ff_4_q);
  D_Flip_Flop d_ff_3 (
    .clk(d_ff_2_qn), .D(d_ff_3_qn), .Q(d_ff_3_q), .Qn(d_ff_3_qn), .reset(and_1_out));  // open: preset, en
  _7_Segment_Display u_7_segment_display_1 (
    .g(dekoder_1_d), .f(dekoder_1_c), .a(dekoder_1_b), .b(dekoder_1_a), .e(dekoder_1_e), .d(dekoder_1_f),
    .c(dekoder_1_g));  // open: dp
  D_Flip_Flop d_ff_4 (
    .clk(d_ff_3_qn), .D(d_ff_4_qn), .Q(d_ff_4_q), .Qn(d_ff_4_qn), .reset(and_1_out));  // open: preset, en
endmodule

module Przerzutnik_D (
  input  D,
  input  Clock,
  output Q,
  output NotQ
);

  wire nand_1_out, nand_2_out, nand_3_out;

  nand nand_1 (nand_1_out, D, D);
  nand nand_2 (nand_2_out, D, Clock);
  nand nand_3 (nand_3_out, Clock, nand_1_out);
  nand nand_4 (Q, nand_2_out, NotQ);
  nand nand_5 (NotQ, Q, nand_3_out);
endmodule

module Zadanie_3 (
  input  A,
  input  B,
  output S,
  output C
);

  xor xor_1 (S, B, A);
  and and_1 (C, B, A);
endmodule

module Zadanie4 (
  input  A,
  input  B,
  input  Cin,
  output S,
  output C
);

  wire and_1_out, and_2_out, xor_1_out;

  xor xor_1 (xor_1_out, A, B);
  and and_1 (and_1_out, xor_1_out, Cin);
  and and_2 (and_2_out, A, B);
  xor xor_2 (S, xor_1_out, Cin);
  or or_1 (C, and_1_out, and_2_out);
endmodule

module Zadanie_5 (
  input  A,
  input  B,
  input  C
);

  wire dekoder_1_a, dekoder_1_b, dekoder_1_c, dekoder_1_d, dekoder_1_e, dekoder_1_f, dekoder_1_g,
       zadanie4_1_c, zadanie4_1_s, zadanie4_2_c, zadanie4_2_s, zadanie_3_1_s;

  Zadanie_3 zadanie_3_1 (.A(A), .B(B), .S(zadanie_3_1_s), .C(zadanie_3_1_s));
  Zadanie4 zadanie4_1 (.A(A), .B(B), .Cin(zadanie_3_1_s), .S(zadanie4_1_s), .C(zadanie4_1_c));
  Zadanie4 zadanie4_2 (.A(A), .B(B), .Cin(zadanie4_1_c), .S(zadanie4_2_s), .C(zadanie4_2_c));
  dekoder dekoder_1 (
    .x(zadanie4_2_c), .y(zadanie4_2_s), .w(zadanie4_1_s), .z(zadanie_3_1_s), .a(dekoder_1_a),
    .b(dekoder_1_b), .c(dekoder_1_c), .d(dekoder_1_d), .e(dekoder_1_e), .f(dekoder_1_f), .g(dekoder_1_g));
  _7_Segment_Display u_7_segment_display_1 (
    .g(dekoder_1_d), .f(dekoder_1_c), .a(dekoder_1_b), .b(dekoder_1_a), .e(dekoder_1_e), .d(dekoder_1_f),
    .c(dekoder_1_g));  // open: dp
endmodule

module Zadanie_6 (
  input  in_1,
  output out_2,
  output out_3,
  output out_4,
  output out_5
);

  wire clock_1_out, or_1_out, or_2_out, or_3_out, xnor_1_out, xnor_2_out, xnor_3_out, xnor_4_out;

  Clock clock_1 (.out(clock_1_out));
  or or_1 (or_1_out, or_3_out, out_3);
  xnor xnor_1 (xnor_1_out, out_5, in_1);
  or or_2 (or_2_out, in_1, out_5);
  or or_3 (or_3_out, or_2_out, out_4);
  xnor xnor_2 (xnor_2_out, out_4, or_2_out);
  xnor xnor_3 (xnor_3_out, out_3, or_3_out);
  xnor xnor_4 (xnor_4_out, out_2, or_1_out);
  D_Flip_Flop d_ff_1 (.clk(clock_1_out), .D(xnor_1_out), .Q(out_5));  // open: Qn, preset, en, reset
  D_Flip_Flop d_ff_2 (.clk(clock_1_out), .D(xnor_2_out), .Q(out_4));  // open: Qn, preset, en, reset
  D_Flip_Flop d_ff_3 (.clk(clock_1_out), .D(xnor_3_out), .Q(out_3));  // open: Qn, preset, en, reset
  D_Flip_Flop d_ff_4 (.clk(clock_1_out), .D(xnor_4_out), .Q(out_2));  // open: Qn, preset, en, reset
endmodule

module Zadanie_7 (
  input  Zezwolenie,
  input  Zmiana_kierunku,
  output q0,
  output q1,
  output q2,
  output q3
);

  wire and_1_out, and_2_out, and_3_out, xor_1_out, xor_2_out, xor_3_out, xor_4_out, xor_5_out, xor_6_out,
       xor_7_out, zegar_out;

  xor xor_1 (xor_1_out, Zmiana_kierunku, q0);
  and and_1 (and_1_out, Zezwolenie, xor_1_out);
  xor xor_2 (xor_2_out, q1, Zmiana_kierunku);
  and and_2 (and_2_out, and_1_out, xor_2_out);
  xor xor_3 (xor_3_out, q2, Zmiana_kierunku);
  and and_3 (and_3_out, and_2_out, xor_3_out);
  xor xor_4 (xor_4_out, q0, Zezwolenie);
  xor xor_5 (xor_5_out, q1, and_1_out);
  xor xor_6 (xor_6_out, q2, and_2_out);
  xor xor_7 (xor_7_out, q3, and_3_out);
  Clock zegar (.out(zegar_out));
  D_Flip_Flop d_ff_1 (.clk(zegar_out), .D(xor_4_out), .Q(q0));  // open: Qn, preset, en, reset
  D_Flip_Flop d_ff_2 (.clk(zegar_out), .D(xor_5_out), .Q(q1));  // open: Qn, preset, en, reset
  D_Flip_Flop d_ff_3 (.clk(zegar_out), .D(xor_6_out), .Q(q2));  // open: Qn, preset, en, reset
  D_Flip_Flop d_ff_4 (.clk(zegar_out), .D(xor_7_out), .Q(q3));  // open: Qn, preset, en, reset
endmodule

module Zadanie_8_pomoc (
  input  zegar,
  input  Zezwolenie,
  input  Zmiana_kierunku,
  output q0,
  output q1,
  output q2,
  output q3
);

  wire and_1_out, and_2_out, and_3_out, xor_1_out, xor_2_out, xor_3_out, xor_4_out, xor_5_out, xor_6_out,
       xor_7_out;

  xor xor_1 (xor_1_out, Zmiana_kierunku, q0);
  and and_1 (and_1_out, Zezwolenie, xor_1_out);
  xor xor_2 (xor_2_out, q1, Zmiana_kierunku);
  and and_2 (and_2_out, and_1_out, xor_2_out);
  xor xor_3 (xor_3_out, q2, Zmiana_kierunku);
  and and_3 (and_3_out, and_2_out, xor_3_out);
  xor xor_4 (xor_4_out, q0, Zezwolenie);
  xor xor_5 (xor_5_out, q1, and_1_out);
  xor xor_6 (xor_6_out, q2, and_2_out);
  xor xor_7 (xor_7_out, q3, and_3_out);
  D_Flip_Flop d_ff_1 (.clk(zegar), .D(xor_4_out), .Q(q0));  // open: Qn, preset, en, reset
  D_Flip_Flop d_ff_2 (.clk(zegar), .D(xor_5_out), .Q(q1));  // open: Qn, preset, en, reset
  D_Flip_Flop d_ff_3 (.clk(zegar), .D(xor_6_out), .Q(q2));  // open: Qn, preset, en, reset
  D_Flip_Flop d_ff_4 (.clk(zegar), .D(xor_7_out), .Q(q3));  // open: Qn, preset, en, reset
endmodule

module Zadanie_8 (
  input  zmiana_kierunku,
  input  zezwolenie
);

  wire clock_1_out, dekoder_1_a, dekoder_1_b, dekoder_1_c, dekoder_1_d, dekoder_1_e, dekoder_1_f,
       dekoder_1_g, zadanie_8_pomoc_1_q0, zadanie_8_pomoc_1_q1, zadanie_8_pomoc_1_q2, zadanie_8_pomoc_1_q3;

  Clock clock_1 (.out(clock_1_out));
  Zadanie_8_pomoc zadanie_8_pomoc_1 (
    .zegar(clock_1_out), .Zezwolenie(zezwolenie), .Zmiana_kierunku(zmiana_kierunku),
    .q0(zadanie_8_pomoc_1_q0), .q1(zadanie_8_pomoc_1_q1), .q2(zadanie_8_pomoc_1_q2), .q3(zadanie_8_pomoc_1_q3));
  dekoder dekoder_1 (
    .x(zadanie_8_pomoc_1_q3), .y(zadanie_8_pomoc_1_q2), .w(zadanie_8_pomoc_1_q1), .z(zadanie_8_pomoc_1_q0),
    .a(dekoder_1_a), .b(dekoder_1_b), .c(dekoder_1_c), .d(dekoder_1_d), .e(dekoder_1_e), .f(dekoder_1_f),
    .g(dekoder_1_g));
  _7_Segment_Display u_7_segment_display_1 (
    .g(dekoder_1_d), .f(dekoder_1_c), .a(dekoder_1_b), .b(dekoder_1_a), .e(dekoder_1_e), .d(dekoder_1_f),
    .c(dekoder_1_g));  // open: dp
endmodule

module Zadanie_9 (
  input  A,
  input  B,
  input  C,
  input  Sterujace,
  output y0,
  output y1,
  output y2,
  output y3,
  output y4,
  output y5,
  output y6,
  output y7
);

  wire not_1_out, not_2_out, not_3_out;

  not not_1 (not_1_out, B);
  not not_2 (not_2_out, A);
  not not_3 (not_3_out, C);
  and and_1 (y0, not_3_out, Sterujace, not_1_out, not_2_out);
  and and_2 (y1, not_2_out, not_1_out, Sterujace, C);
  and and_3 (y2, not_2_out, Sterujace, B, not_3_out);
  and and_4 (y3, not_2_out, Sterujace, B, C);
  and and_5 (y4, A, not_1_out, not_3_out, Sterujace);
  and and_6 (y5, A, not_1_out, Sterujace, C);
  and and_7 (y6, A, B, Sterujace, not_3_out);
  and and_8 (y7, A, B, C, Sterujace);
endmodule

module Zadanie_10 (
  input  A,
  input  B,
  input  Cin,
  input  Wlacznie,
  output S,
  output Cout
);

  wire zadanie_9_1_y0, zadanie_9_1_y1, zadanie_9_1_y2, zadanie_9_1_y3, zadanie_9_1_y4, zadanie_9_1_y5,
       zadanie_9_1_y6, zadanie_9_1_y7;

  Zadanie_9 zadanie_9_1 (
    .A(A), .B(B), .C(Cin), .Sterujace(Wlacznie), .y0(zadanie_9_1_y0), .y1(zadanie_9_1_y1),
    .y2(zadanie_9_1_y2), .y3(zadanie_9_1_y3), .y4(zadanie_9_1_y4), .y5(zadanie_9_1_y5), .y6(zadanie_9_1_y6),
    .y7(zadanie_9_1_y7));
  or or_1 (S, zadanie_9_1_y1, zadanie_9_1_y2, zadanie_9_1_y4, zadanie_9_1_y7);
  or or_2 (Cout, zadanie_9_1_y3, zadanie_9_1_y5, zadanie_9_1_y6, zadanie_9_1_y7);
endmodule

module Zadanie_11 (
  input  x7,
  input  x6,
  input  x5,
  input  x4,
  input  x3,
  input  x2,
  input  x1,
  input  x0,
  input  s0,
  input  s1,
  input  s2,
  output Y
);

  wire and_1_out, and_2_out, and_3_out, and_4_out, and_5_out, and_6_out, and_7_out, and_8_out, not_1_out,
       not_2_out, not_3_out;

  and and_1 (and_1_out, not_3_out, s1, s0, x6);
  and and_2 (and_2_out, s2, s1, s0, x7);
  and and_3 (and_3_out, s2, not_2_out, s0, x5);
  and and_4 (and_4_out, not_3_out, s0, not_2_out, x4);
  or or_1 (Y, and_2_out, and_1_out, and_3_out, and_4_out, and_5_out, and_6_out, and_7_out, and_8_out);
  and and_5 (and_5_out, s2, s1, not_1_out, x3);
  and and_6 (and_6_out, not_3_out, s1, not_1_out, x2);
  and and_7 (and_7_out, s2, not_2_out, not_1_out, x1);
  and and_8 (and_8_out, not_3_out, not_2_out, not_1_out, x0);
  not not_1 (not_1_out, s0);
  not not_2 (not_2_out, s1);
  not not_3 (not_3_out, s2);
endmodule

module Zadanie_12 (
  input  a,
  input  b,
  input  s1,
  input  s0,
  output y
);

  wire and_1_out, and_2_out, and_3_out, and_4_out, and_5_out, and_6_out, xnor_1_out, xor_1_out;

  and and_1 (and_1_out, a, ~b);  // AND_Gate
  and and_2 (and_2_out, ~a, b);  // AND_Gate
  xor xor_1 (xor_1_out, a, b);
  xnor xnor_1 (xnor_1_out, b, a);
  and and_3 (and_3_out, ~s1, ~s0, xor_1_out);  // AND_Gate
  and and_4 (and_4_out, ~s1, s0, xnor_1_out);  // AND_Gate
  and and_5 (and_5_out, s1, ~s0, and_1_out);  // AND_Gate
  and and_6 (and_6_out, s1, s0, and_2_out);
  or or_1 (y, and_3_out, and_4_out, and_5_out, and_6_out);
endmodule

module Multiplekser (
  input  z,
  input  w,
  input  y,
  input  x,
  input  s1,
  input  s0,
  output y_2
);

  wire and_1_out, and_2_out, and_3_out, and_4_out;

  and and_1 (and_1_out, ~s0, ~s1, x);  // AND_Gate
  and and_2 (and_2_out, s0, ~s1, y);  // AND_Gate
  and and_3 (and_3_out, ~s0, s1, w);  // AND_Gate
  and and_4 (and_4_out, s0, s1, z);
  or or_1 (y_2, and_1_out, and_2_out, and_3_out, and_4_out);
endmodule

module Zadanie_13 (
  input  z0,
  input  w0,
  input  y0,
  input  x0,
  input  z0_2,
  input  w0_2,
  input  y0_2,
  input  x1,
  input  s0,
  input  s1,
  output out_11,
  output out_12
);

  Multiplekser multiplekser_1 (.z(z0), .w(w0), .y(y0), .x(x0), .s1(s1), .s0(s0), .y_2(out_11));
  Multiplekser multiplekser_2 (.z(z0_2), .w(w0_2), .y(y0_2), .x(x1), .s1(s1), .s0(s0), .y_2(out_12));
endmodule
