// Logisim project Zadanie 1.circ as structural Verilog: 15 circuits, main circuit main
module main (
  input  in_1,
  input  in_2,
  input  in_3,
  input  in_4
);

  wire dekoder_1_a, dekoder_1_b, dekoder_1_c, dekoder_1_d, dekoder_1_e, dekoder_1_f, dekoder_1_g;

  dekoder dekoder_1 (
    .x(in_1), .y(in_2), .w(in_3), .z(in_4), .a(dekoder_1_a), .b(dekoder_1_b), .c(dekoder_1_c),
    .d(dekoder_1_d), .e(dekoder_1_e), .f(dekoder_1_f), .g(dekoder_1_g));
  _7_Segment_Display u_7_segment_display_1 (
    .g(dekoder_1_d), .f(dekoder_1_c), .a(dekoder_1_b), .b(dekoder_1_a), .e(dekoder_1_e), .d(dekoder_1_f),
    .c(dekoder_1_g));  // open: dp
endmodule

module a (
  input  x,
  input  y,
  input  w,
  input  z,
  output out_5
);

  wire or_1_out, or_2_out;

  or or_1 (or_1_out, x, ~y, w, ~z);  // OR_Gate
  or or_2 (or_2_out, x, ~y, ~w, z);  // OR_Gate
  and and_1 (out_5, or_1_out, or_2_out);
endmodule

module dekoder (
  input  x,
  input  y,
  input  w,
  input  z,
  output a,
  output b,
  output c,
  output d,
  output e,
  output f,
  output g
);

  a a_1 (.x(x), .y(y), .w(w), .z(z), .out_5(a));
  b b_1 (.x(x), .y(y), .w(w), .z(z), .out_5(b));
  c c_1 (.x(x), .y(y), .w(w), .z(z), .out_5(c));
  d d_1 (.x(x), .y(y), .w(w), .z(z), .out_5(d));
  e e_1 (.x(x), .y(y), .w(w), .z(z), .out_5(e));
  f f_1 (.x(x), .y(y), .w(w), .z(z), .out_5(f));
  g g_1 (.x(x), .y(y), .w(w), .z(z), .out_5(g));
endmodule

module b (
  input  x,
  input  y,
  input  w,
  input  z,
  output out_5
);

  wire or_1_out, or_2_out;

  or or_1 (or_1_out, x, ~y, w, z);  // OR_Gate
  or or_2 (or_2_out, x, y, w, ~z);  // OR_Gate
  and and_1 (out_5, or_1_out, or_2_out);
endmodule

module c (
  input  x,
  input  y,
  input  w,
  input  z,
  output out_5
);

  wire and_1_out, and_2_out, and_3_out;

  and and_1 (and_1_out, ~w, ~z);  // AND_Gate
  and and_2 (and_2_out, y, ~w);  // AND_Gate
  and and_3 (and_3_out, y, ~z);  // AND_Gate
  or or_1 (out_5, x, and_1_out, and_2_out, and_3_out);
endmodule

module d (
  input  x,
  input  y,
  input  w,
  input  z,
  output out_5
);

  wire and_1_out, and_2_out, and_3_out;

  and and_1 (and_1_out, ~y, w);  // AND_Gate
  and and_2 (and_2_out, w, ~z);  // AND_Gate
  and and_3 (and_3_out, y, ~w);  // AND_Gate
  or or_1 (out_5, x, and_1_out, and_2_out, and_3_out);
endmodule

module e (
  input  x,
  input  y,
  input  w,
  input  z,
  output out_5
);

  wire and_1_out, and_2_out;

  and and_1 (and_1_out, ~y, ~z);  // AND_Gate
  and and_2 (and_2_out, w, ~z);  // AND_Gate
  or or_1 (out_5, and_1_out, and_2_out);
endmodule

module f (
  input  x,
  input  y,
  input  w,
  input  z,
  output out_5
);

  wire and_1_out, and_2_out, and_3_out, and_4_out;

  and and_1 (and_1_out, ~y, ~z);  // AND_Gate
  and and_2 (and_2_out, ~y, w);  // AND_Gate
  and and_3 (and_3_out, w, ~z);  // AND_Gate
  and and_4 (and_4_out, y, ~w, z);  // AND_Gate
  or or_1 (out_5, x, and_1_out, and_2_out, and_3_out, and_4_out);
endmodule

module g (
  input  x,
  input  y,
  input  w,
  input  z,
  output out_5
);

  or or_1 (out_5, ~w, z, y);  // OR_Gate
endmodule

module Zadanie_2 (
  input  d0,
  input  d1,
  input  d2,
  input  d3
);

  wire clock_1_out, dekoder_1_a, dekoder_1_b, dekoder_1_c, dekoder_1_d, dekoder_1_e, dekoder_1_f,
       dekoder_1_g, przerzutnik_d_1_q, przerzutnik_d_2_q, przerzutnik_d_3_q, przerzutnik_d_4_q;

  Clock clock_1 (.out(clock_1_out));
  Przerzutnik_D przerzutnik_d_1 (.Clock(clock_1_out), .En(d0), .Q(przerzutnik_d_1_q));  // open: nQ
  Przerzutnik_D przerzutnik_d_2 (.Clock(clock_1_out), .En(d1), .Q(przerzutnik_d_2_q));  // open: nQ
  Przerzutnik_D przerzutnik_d_3 (.Clock(clock_1_out), .En(d2), .Q(przerzutnik_d_3_q));  // open: nQ
  Przerzutnik_D przerzutnik_d_4 (.Clock(clock_1_out), .En(d3), .Q(przerzutnik_d_4_q));  // open: nQ
  dekoder dekoder_1 (
    .x(przerzutnik_d_1_q), .y(przerzutnik_d_2_q), .w(przerzutnik_d_3_q), .z(przerzutnik_d_4_q),
    .a(dekoder_1_a), .b(dekoder_1_b), .c(dekoder_1_c), .d(dekoder_1_d), .e(dekoder_1_e), .f(dekoder_1_f),
    .g(dekoder_1_g));
  _7_Segment_Display u_7_segment_display_1 (
    .g(dekoder_1_d), .f(dekoder_1_c), .a(dekoder_1_b), .b(dekoder_1_a), .e(dekoder_1_e), .d(dekoder_1_f),
    .c(dekoder_1_g));  // open: dp
endmodule

module Przerzutnik_D (
  input  Clock,
  input  En,
  output Q,
  output nQ
);

  wire and_1_out, and_2_out, and_3_out, and_4_out;

  and and_1 (and_1_out, and_4_out, and_2_out);
  and and_2 (and_2_out, and_1_out, Clock);
  and and_3 (and_3_out, and_2_out, Clock, and_4_out);
  and and_4 (and_4_out, and_3_out, En);
  and and_5 (Q, and_2_out, nQ);
  and and_6 (nQ, Q, and_3_out);
endmodule

module Zadanie_3 (
  input  a,
  input  b,
  output S,
  output C
);

  xor xor_1 (S, a, b);
  and and_1 (C, a, b);
endmodule

module Zadanie_4 (
  input  a,
  input  b,
  input  Cin,
  output SUM,
  output C
);

  wire and_1_out, and_2_out, xor_1_out;

  and and_1 (and_1_out, a, b);
  xor xor_1 (xor_1_out, a, b);
  and and_2 (and_2_out, xor_1_out, Cin);
  xor xor_2 (SUM, xor_1_out, Cin);
  or or_1 (C, and_2_out, and_1_out);
endmodule

module Zadanie_5 (
  input  b0,
  input  b1,
  input  b2,
  input  a0,
  input  a1,
  input  a2
);

  wire dekoder_1_a, dekoder_1_b, dekoder_1_c, dekoder_1_d, dekoder_1_e, dekoder_1_f, dekoder_1_g,
       zadanie_3_1_c, zadanie_3_1_s, zadanie_4_1_c, zadanie_4_1_sum, zadanie_4_2_c, zadanie_4_2_sum;

  Zadanie_3 zadanie_3_1 (.a(a0), .b(b0), .S(zadanie_3_1_s), .C(zadanie_3_1_c));
  Zadanie_4 zadanie_4_1 (.a(a1), .b(b1), .Cin(zadanie_3_1_c), .SUM(zadanie_4_1_sum), .C(zadanie_4_1_c));
  Zadanie_4 zadanie_4_2 (.a(a2), .b(b2), .Cin(zadanie_4_1_c), .SUM(zadanie_4_2_sum), .C(zadanie_4_2_c));
  dekoder dekoder_1 (
    .x(zadanie_4_2_c), .y(zadanie_4_2_sum), .w(zadanie_4_1_sum), .z(zadanie_3_1_s), .a(dekoder_1_a),
    .b(dekoder_1_b), .c(dekoder_1_c), .d(dekoder_1_d), .e(dekoder_1_e), .f(dekoder_1_f), .g(dekoder_1_g));
  _7_Segment_Display u_7_segment_display_1 (
    .g(dekoder_1_d), .f(dekoder_1_c), .a(dekoder_1_b), .b(dekoder_1_a), .e(dekoder_1_e), .d(dekoder_1_f),
    .c(dekoder_1_g));  // open: dp
endmodule

module Zadanie_6 (
  input  in_1
);

  wire d_ff_1_q, d_ff_1_qn, d_ff_2_q, d_ff_2_qn, d_ff_3_q, d_ff_3_qn, d_ff_4_q, d_ff_4_qn, dekoder_1_a,
       dekoder_1_b, dekoder_1_c, dekoder_1_d, dekoder_1_e, dekoder_1_f, dekoder_1_g;

  Clock clock_1 ();  // open: out
  D_Flip_Flop d_ff_1 (.clk(in_1), .D(d_ff_1_qn), .Q(d_ff_1_q), .Qn(d_ff_1_qn));  // open: preset, en, reset
  D_Flip_Flop d_ff_2 (.clk(d_ff_1_q), .D(d_ff_2_qn), .Q(d_ff_2_q), .Qn(d_ff_2_qn));  // open: preset, en, reset
  D_Flip_Flop d_ff_3 (.clk(d_ff_2_q), .D(d_ff_3_qn), .Q(d_ff_3_q), .Qn(d_ff_3_qn));  // open: preset, en, reset
  D_Flip_Flop d_ff_4 (.clk(d_ff_3_q), .D(d_ff_4_qn), .Q(d_ff_4_q), .Qn(d_ff_4_qn));  // open: preset, en, reset
  dekoder dekoder_1 (
    .x(d_ff_4_q), .y(d_ff_3_q), .w(d_ff_2_q), .z(d_ff_1_q), .a(dekoder_1_a), .b(dekoder_1_b),
    .c(dekoder_1_c), .d(dekoder_1_d), .e(dekoder_1_e), .f(dekoder_1_f), .g(dekoder_1_g));
  _7_Segment_Display u_7_segment_display_1 (
    .g(dekoder_1_d), .f(dekoder_1_c), .a(dekoder_1_b), .b(dekoder_1_a), .e(dekoder_1_e), .d(dekoder_1_f),
    .c(dekoder_1_g));  // open: dp
endmodule
